// Logisim project control_logic.circ as structural Verilog: 1 circuit, main circuit control_logic
module control_logic (
  input  [31:0] inst,
  input  BrEq,
  input  BrLt,
  output PCSel,
  output RegWEn,
  output [2:0] ImmSel,
  output BrUn,
  output ASel,
  output BSel,
  output [3:0] ALUSel,
  output MemRW,
  output [1:0] WBSel,
  output CSRSel,
  output CSRWen
);

  ROM #(.addrWidth(11), .dataWidth(15)) rom_1 (
    .addr({inst[30], inst[14:12], inst[6:2], BrEq, BrLt}),
    .data({PCSel, RegWEn, ImmSel, BrUn, ASel, BSel, ALUSel, MemRW, WBSel}));

  // Other names for the same wires on the sheet: ROM_addr[10:0] = {inst[30], inst[14:12], inst[6:2], BrEq, BrLt}

  // Notes on the sheet:
  //   INPUTS to your circuit
  //   contents of rom_1 (hex, n*v repeats v):
  //   16*0 4*2481 1020*0 4*2481
  //   DON'T CHANGE THE LOCATIONS OF THE INPUTS AND OUTPUTS!
  //   OUTPUT from your circuit
endmodule
