// Logisim project imm_gen.circ as structural Verilog: 2 circuits, main circuit imm_gen
module imm_gen (
  input  [31:0] inst,
  input  [2:0] ImmSel,
  output [31:0] imm
);

  immediate_generator immediate_generator_1 (.inst(inst), .ImmSel(ImmSel), .imm(imm));

  // Notes on the sheet:
  //   INPUTS to your circuit
  //   DON'T CHANGE THE LOCATIONS OF THE INPUTS AND OUTPUTS!
  //   OUTPUT from your circuit
endmodule

module immediate_generator (
  input  [31:0] inst,
  input  [2:0] ImmSel,
  output [31:0] imm
);

  assign imm = {{20{inst[31]}}, inst[31:20]};  // Bit_Extender bit_extender_1

  // Other names for the same wires on the sheet: i_type[11:0] = inst[31:20]
endmodule
