// Logisim project regfile.circ as structural Verilog: 2 circuits, main circuit regfile
module regfile (
  input  [4:0] rs1,
  input  [4:0] rs2,
  input  [4:0] rd,
  input  [31:0] Write_Data,
  input  RegWEn,
  input  clk,
  output [31:0] ra,
  output [31:0] sp,
  output [31:0] t0,
  output [31:0] t1,
  output [31:0] t2,
  output [31:0] s0,
  output [31:0] s1,
  output [31:0] a0,
  output [31:0] Read_Data_1,
  output [31:0] Read_Data_2
);

  register_file register_file_1 (
    .write_data(Write_Data), .clk(clk), .write_en(RegWEn), .write_rd(rd), .read1(rs1), .read2(rs2),
    .rs1(Read_Data_1), .rs2(Read_Data_2), .ra(ra), .sp(sp), .t0(t0), .t1(t1), .t2(t2), .s0(s0), .s1(s1),
    .a0(a0));

  // Other names for the same wires on the sheet: read_data1[31:0] = Read_Data_1; read_data2[31:0] = Read_Data_2;
  //   read_reg1[4:0] = rs1; read_reg2[4:0] = rs2; write_en = RegWEn; write_reg[4:0] = rd

  // Notes on the sheet:
  //   INPUTS to your circuit
  //   DON'T CHANGE THE LOCATIONS OF THE INPUTS AND OUTPUTS!
  //   These are DEBUG/TEST outputs from your circuit.
  //   OUTPUTS from your circuit
endmodule

module register_file (
  input  [31:0] write_data,
  input  clk,
  input  write_en,
  input  [4:0] write_rd,
  input  [4:0] read1,
  input  [4:0] read2,
  output [31:0] rs1,
  output [31:0] rs2,
  output [31:0] ra,
  output [31:0] sp,
  output [31:0] t0,
  output [31:0] t1,
  output [31:0] t2,
  output [31:0] s0,
  output [31:0] s1,
  output [31:0] a0
);

  wire wr1, wr2, wr3, wr4, wr5, wr6, wr7, wr8, wr9, wr10, wr11, wr12, wr13, wr14, wr15, wr16, wr17, wr18,
       wr19, wr20, wr21, wr22, wr23, wr24, wr25, wr26, wr27, wr28, wr29, wr30, wr31;
  wire [31:0] x3, x4, x11, x12, x13, x14, x15, x16, x17, x18, x19, x20, x21, x22, x23, x24, x25, x26, x27,
       x28, x29, x30, x31;

  Decoder #(.select(5)) decoder_1 (
    .out1(wr1), .out2(wr2), .out3(wr3), .out4(wr4), .out5(wr5), .out6(wr6), .out7(wr7), .out8(wr8),
    .out9(wr9), .out10(wr10), .out11(wr11), .out12(wr12), .out13(wr13), .out14(wr14), .out15(wr15),
    .out16(wr16), .out17(wr17), .out18(wr18), .out19(wr19), .out20(wr20), .out21(wr21), .out22(wr22),
    .out23(wr23), .out24(wr24), .out25(wr25), .out26(wr26), .out27(wr27), .out28(wr28), .out29(wr29),
    .out30(wr30), .out31(wr31), .sel(write_rd), .en(write_en));  // open: out0
  Multiplexer #(.enable("false"), .select(5), .width(32)) multiplexer_1 (
    .in0({32{1'b0}}), .in1(ra), .in2(sp), .in3(x3), .in4(x4), .in5(t0), .in6(t1), .in7(t2), .in8(s0),
    .in9(s1), .in10(a0), .in11(x11), .in12(x12), .in13(x13), .in14(x14), .in15(x15), .in16(x16), .in17(x17),
    .in18(x18), .in19(x19), .in20(x20), .in21(x21), .in22(x22), .in23(x23), .in24(x24), .in25(x25),
    .in26(x26), .in27(x27), .in28(x28), .in29(x29), .in30(x30), .in31(x31), .out(rs1), .sel(read1));
  Register #(.width(32)) register_1 (.D(write_data), .en(wr1), .clk(clk), .Q(ra));  // open: clr
  Register #(.width(32)) register_2 (.D(write_data), .en(wr5), .clk(clk), .Q(t0));  // open: clr
  Register #(.width(32)) register_3 (.D(write_data), .en(wr9), .clk(clk), .Q(s1));  // open: clr
  Register #(.width(32)) register_4 (.D(write_data), .en(wr13), .clk(clk), .Q(x13));  // open: clr
  Register #(.width(32)) register_5 (.D(write_data), .en(wr17), .clk(clk), .Q(x17));  // open: clr
  Register #(.width(32)) register_6 (.D(write_data), .en(wr21), .clk(clk), .Q(x21));  // open: clr
  Register #(.width(32)) register_7 (.D(write_data), .en(wr25), .clk(clk), .Q(x25));  // open: clr
  Register #(.width(32)) register_8 (.D(write_data), .en(wr29), .clk(clk), .Q(x29));  // open: clr
  Multiplexer #(.enable("false"), .select(5), .width(32)) multiplexer_2 (
    .in0({32{1'b0}}), .in1(ra), .in2(sp), .in3(x3), .in4(x4), .in5(t0), .in6(t1), .in7(t2), .in8(s0),
    .in9(s1), .in10(a0), .in11(x11), .in12(x12), .in13(x13), .in14(x14), .in15(x15), .in16(x16), .in17(x17),
    .in18(x18), .in19(x19), .in20(x20), .in21(x21), .in22(x22), .in23(x23), .in24(x24), .in25(x25),
    .in26(x26), .in27(x27), .in28(x28), .in29(x29), .in30(x30), .in31(x31), .out(rs2), .sel(read2));
  Register #(.width(32)) register_9 (.D(write_data), .en(wr2), .clk(clk), .Q(sp));  // open: clr
  Register #(.width(32)) register_10 (.D(write_data), .en(wr6), .clk(clk), .Q(t1));  // open: clr
  Register #(.width(32)) register_11 (.D(write_data), .en(wr10), .clk(clk), .Q(a0));  // open: clr
  Register #(.width(32)) register_12 (.D(write_data), .en(wr14), .clk(clk), .Q(x14));  // open: clr
  Register #(.width(32)) register_13 (.D(write_data), .en(wr18), .clk(clk), .Q(x18));  // open: clr
  Register #(.width(32)) register_14 (.D(write_data), .en(wr22), .clk(clk), .Q(x22));  // open: clr
  Register #(.width(32)) register_15 (.D(write_data), .en(wr26), .clk(clk), .Q(x26));  // open: clr
  Register #(.width(32)) register_16 (.D(write_data), .en(wr30), .clk(clk), .Q(x30));  // open: clr
  Register #(.width(32)) register_17 (.D(write_data), .en(wr3), .clk(clk), .Q(x3));  // open: clr
  Register #(.width(32)) register_18 (.D(write_data), .en(wr7), .clk(clk), .Q(t2));  // open: clr
  Register #(.width(32)) register_19 (.D(write_data), .en(wr11), .clk(clk), .Q(x11));  // open: clr
  Register #(.width(32)) register_20 (.D(write_data), .en(wr15), .clk(clk), .Q(x15));  // open: clr
  Register #(.width(32)) register_21 (.D(write_data), .en(wr19), .clk(clk), .Q(x19));  // open: clr
  Register #(.width(32)) register_22 (.D(write_data), .en(wr23), .clk(clk), .Q(x23));  // open: clr
  Register #(.width(32)) register_23 (.D(write_data), .en(wr27), .clk(clk), .Q(x27));  // open: clr
  Register #(.width(32)) register_24 (.D(write_data), .en(wr31), .clk(clk), .Q(x31));  // open: clr
  Register #(.width(32)) register_25 (.D(write_data), .en(wr4), .clk(clk), .Q(x4));  // open: clr
  Register #(.width(32)) register_26 (.D(write_data), .en(wr8), .clk(clk), .Q(s0));  // open: clr
  Register #(.width(32)) register_27 (.D(write_data), .en(wr12), .clk(clk), .Q(x12));  // open: clr
  Register #(.width(32)) register_28 (.D(write_data), .en(wr16), .clk(clk), .Q(x16));  // open: clr
  Register #(.width(32)) register_29 (.D(write_data), .en(wr20), .clk(clk), .Q(x20));  // open: clr
  Register #(.width(32)) register_30 (.D(write_data), .en(wr24), .clk(clk), .Q(x24));  // open: clr
  Register #(.width(32)) register_31 (.D(write_data), .en(wr28), .clk(clk), .Q(x28));  // open: clr

  // Other names for the same wires on the sheet: x1[31:0] = ra; x2[31:0] = sp; x5[31:0] = t0; x6[31:0] = t1;
  //   x7[31:0] = t2; x8[31:0] = s0; x9[31:0] = s1; x10[31:0] = a0

  // Notes on the sheet:
  //   These are DEBUG/TEST outputs from your circuit.
endmodule
