// Logisim project alu.circ as structural Verilog: 12 circuits, main circuit alu
module alu (
  input  [31:0] A,
  input  [31:0] B,
  input  [3:0] ALUSel,
  output [31:0] Result
);

  wire comparator_1_lt, comparator_2_lt;
  wire [31:0] add0, ander1, mul10, mulh14, mulhu11, orer2, sll6, slt7, sltu8, sra5, srl4, sub12, xorer3;

  Multiplexer #(.enable("false"), .select(4), .width(32)) multiplexer_1 (
    .in0(add0), .in1(ander1), .in2(orer2), .in3(xorer3), .in4(srl4), .in5(sra5), .in6(sll6), .in7(slt7),
    .in8(sltu8), .in10(mul10), .in11(mulhu11), .in12(sub12), .in13(B), .in14(mulh14), .out(Result),
    .sel(ALUSel));  // open: in9, in15
  Adder #(.width(32)) adder_1 (.a(A), .b(B), .out(add0));  // open: cin, cout
  Shifter #(.shift("lr"), .width(32)) shifter_1 (.in(A), .\dist (B[4:0]), .out(srl4));
  Shifter #(.shift("ar"), .width(32)) shifter_2 (.in(A), .\dist (B[4:0]), .out(sra5));
  Shifter #(.width(32)) shifter_3 (.in(A), .\dist (B[4:0]), .out(sll6));
  Comparator #(.width(32)) comparator_1 (.a(A), .b(B), .lt(comparator_1_lt));  // open: gt, eq
  Multiplier #(.width(32)) multiplier_1 (.a(A), .b(B), .out(mul10));  // open: cin, cout
  Subtractor #(.width(32)) subtractor_1 (.a(A), .b(B), .out(sub12));  // open: bin, bout
  ander ander_1 (.in_1(A), .in_2(B), .out_3(ander1));
  orer orer_1 (.in_1(A), .in_2(B), .out_3(orer2));
  xorer xorer_1 (.in_1(A), .in_2(B), .out_3(xorer3));
  assign slt7 = {{31{1'b0}}, comparator_1_lt};  // Bit_Extender bit_extender_1
  multiplier_mulhu multiplier_mulhu_1 (.in_1(A), .in_2(B), .out_3(mulhu11));
  multiplier_mulu multiplier_mulu_1 (.in_1(A), .in_2(B), .out_3(mulh14));
  Comparator #(.mode("unsigned"), .width(32)) comparator_2 (.a(A), .b(B), .lt(comparator_2_lt));  // open: gt, eq
  assign sltu8 = {{31{1'b0}}, comparator_2_lt};  // Bit_Extender bit_extender_2

  // Other names for the same wires on the sheet: bsel13[31:0] = B

  // Notes on the sheet:
  //   INPUTS to your circuit
  //   DON'T CHANGE THE LOCATIONS OF THE INPUTS AND OUTPUTS!
  //   OUTPUT from your circuit
endmodule

module ander_4bit (
  input  [3:0] in_1,
  input  [3:0] in_2,
  output [3:0] out_3
);

  and and_1 (out_3[0], in_1[0], in_2[0]);
  and and_2 (out_3[1], in_1[1], in_2[1]);
  and and_3 (out_3[2], in_1[2], in_2[2]);
  and and_4 (out_3[3], in_1[3], in_2[3]);
endmodule

module ander_16bit (
  input  [15:0] in_1,
  input  [15:0] in_2,
  output [15:0] out_3
);

  ander_4bit ander_4bit_1 (.in_1(in_1[3:0]), .in_2(in_2[3:0]), .out_3(out_3[3:0]));
  ander_4bit ander_4bit_2 (.in_1(in_1[7:4]), .in_2(in_2[7:4]), .out_3(out_3[7:4]));
  ander_4bit ander_4bit_3 (.in_1(in_1[11:8]), .in_2(in_2[11:8]), .out_3(out_3[11:8]));
  ander_4bit ander_4bit_4 (.in_1(in_1[15:12]), .in_2(in_2[15:12]), .out_3(out_3[15:12]));
endmodule

module ander (
  input  [31:0] in_1,
  input  [31:0] in_2,
  output [31:0] out_3
);

  ander_16bit ander_16bit_1 (.in_1(in_1[15:0]), .in_2(in_2[15:0]), .out_3(out_3[15:0]));
  ander_16bit ander_16bit_2 (.in_1(in_1[31:16]), .in_2(in_2[31:16]), .out_3(out_3[31:16]));
endmodule

module orer_4bit (
  input  [3:0] in_1,
  input  [3:0] in_2,
  output [3:0] out_3
);

  or or_1 (out_3[0], in_1[0], in_2[0]);
  or or_2 (out_3[1], in_1[1], in_2[1]);
  or or_3 (out_3[2], in_1[2], in_2[2]);
  or or_4 (out_3[3], in_1[3], in_2[3]);
endmodule

module orer_16bit (
  input  [15:0] in_1,
  input  [15:0] in_2,
  output [15:0] out_3
);

  orer_4bit orer_4bit_1 (.in_1(in_1[3:0]), .in_2(in_2[3:0]), .out_3(out_3[3:0]));
  orer_4bit orer_4bit_2 (.in_1(in_1[7:4]), .in_2(in_2[7:4]), .out_3(out_3[7:4]));
  orer_4bit orer_4bit_3 (.in_1(in_1[11:8]), .in_2(in_2[11:8]), .out_3(out_3[11:8]));
  orer_4bit orer_4bit_4 (.in_1(in_1[15:12]), .in_2(in_2[15:12]), .out_3(out_3[15:12]));
endmodule

module orer (
  input  [31:0] in_1,
  input  [31:0] in_2,
  output [31:0] out_3
);

  orer_16bit orer_16bit_1 (.in_1(in_1[15:0]), .in_2(in_2[15:0]), .out_3(out_3[15:0]));
  orer_16bit orer_16bit_2 (.in_1(in_1[31:16]), .in_2(in_2[31:16]), .out_3(out_3[31:16]));
endmodule

module xorer_4bit (
  input  [3:0] in_1,
  input  [3:0] in_2,
  output [3:0] out_3
);

  xor xor_1 (out_3[0], in_1[0], in_2[0]);
  xor xor_2 (out_3[1], in_1[1], in_2[1]);
  xor xor_3 (out_3[2], in_1[2], in_2[2]);
  xor xor_4 (out_3[3], in_1[3], in_2[3]);
endmodule

module xorer_16bit (
  input  [15:0] in_1,
  input  [15:0] in_2,
  output [15:0] out_3
);

  xorer_4bit xorer_4bit_1 (.in_1(in_1[3:0]), .in_2(in_2[3:0]), .out_3(out_3[3:0]));
  xorer_4bit xorer_4bit_2 (.in_1(in_1[7:4]), .in_2(in_2[7:4]), .out_3(out_3[7:4]));
  xorer_4bit xorer_4bit_3 (.in_1(in_1[11:8]), .in_2(in_2[11:8]), .out_3(out_3[11:8]));
  xorer_4bit xorer_4bit_4 (.in_1(in_1[15:12]), .in_2(in_2[15:12]), .out_3(out_3[15:12]));
endmodule

module xorer (
  input  [31:0] in_1,
  input  [31:0] in_2,
  output [31:0] out_3
);

  xorer_16bit xorer_16bit_1 (.in_1(in_1[15:0]), .in_2(in_2[15:0]), .out_3(out_3[15:0]));
  xorer_16bit xorer_16bit_2 (.in_1(in_1[31:16]), .in_2(in_2[31:16]), .out_3(out_3[31:16]));
endmodule

module multiplier_mulhu (
  input  [31:0] in_1,
  input  [31:0] in_2,
  output [31:0] out_3
);

  wire [31:0] multiplier_1_out;
  wire [63:0] bit_extender_1_out, bit_extender_2_out;

  assign bit_extender_1_out = {{32{1'b0}}, in_1};  // Bit_Extender bit_extender_1
  assign bit_extender_2_out = {{32{1'b0}}, in_2};  // Bit_Extender bit_extender_2
  Multiplier #(.width(64)) multiplier_1 (
    .a(bit_extender_1_out), .b(bit_extender_2_out), .out({out_3, multiplier_1_out}));  // open: cin, cout
endmodule

module multiplier_mulu (
  input  [31:0] in_1,
  input  [31:0] in_2,
  output [31:0] out_3
);

  wire [31:0] multiplier_1_out;
  wire [63:0] bit_extender_1_out, bit_extender_2_out;

  assign bit_extender_1_out = {{32{in_1[31]}}, in_1};  // Bit_Extender bit_extender_1
  assign bit_extender_2_out = {{32{in_2[31]}}, in_2};  // Bit_Extender bit_extender_2
  Multiplier #(.width(64)) multiplier_1 (
    .a(bit_extender_1_out), .b(bit_extender_2_out), .out({out_3, multiplier_1_out}));  // open: cin, cout
endmodule
