// Logisim project control_logic.circ as structural Verilog: 1 circuit, main circuit control_logic
module control_logic (
  input  [31:0] inst,
  input  BrEq,
  input  BrLt,
  output PCSel,
  output RegWEn,
  output [2:0] ImmSel,
  output BrUn,
  output ASel,
  output BSel,
  output [3:0] ALUSel,
  output MemRW,
  output [1:0] WBSel,
  output CSRSel,
  output CSRWen
);

  wire and_1_out, and_4_out, and_6_out, inst12_and_inst25, mul, mulh, nor_1_out, not_1_out, not_2_out,
       not_inst12_and_inst25, or_2_out, Rtype;
  wire [6:4] rom_1_data;
  wire [10:0] ROM_addr;

  not not_1 (not_1_out, inst[12]);
  nor nor_1 (nor_1_out, inst[2], inst[3]);
  and and_1 (and_1_out, inst[4], inst[5]);
  and and_2 (not_inst12_and_inst25, not_1_out, inst[25]);
  and and_3 (inst12_and_inst25, inst[12], inst[25]);
  ROM #(.addrWidth(11), .dataWidth(15)) rom_1 (
    .addr(ROM_addr),
    .data({PCSel, RegWEn, ImmSel, BrUn, ASel, BSel, rom_1_data[6], ALUSel[2], rom_1_data[4], ALUSel[0], MemRW, WBSel}));
  and and_4 (and_4_out, nor_1_out, and_1_out);
  not not_2 (not_2_out, inst[6]);
  Multiplexer #(.enable("false"), .width(11)) multiplexer_1 (
    .in0({inst[30], inst[14:12], inst[6:2], BrEq, BrLt}), .in1({4'b0000, inst[6:2], 2'b00}), .out(ROM_addr),
    .sel(inst[2]));
  and and_5 (Rtype, and_4_out, not_2_out);
  and and_6 (and_6_out, inst[4], inst[5]);
  and and_7 (CSRWen, and_6_out, inst[6]);
  and and_8 (mul, Rtype, not_inst12_and_inst25);
  and and_9 (mulh, Rtype, inst12_and_inst25);
  or or_1 (ALUSel[1], rom_1_data[4], mul);
  or or_2 (or_2_out, mul, rom_1_data[6]);
  or or_3 (ALUSel[3], mulh, or_2_out);

  assign CSRSel = inst[14];

  // Other names for the same wires on the sheet: nonU_addr[10:0] = {inst[30], inst[14:12], inst[6:2], BrEq, BrLt};
  //   inst_2 = inst[2]; opcode[4:0] = inst[6:2]; U_addr[6:2] = inst[6:2]

  // Notes on the sheet:
  //   INPUTS to your circuit
  //   contents of rom_1 (hex, n*v repeats v):
  //   4*2480 12*0 4*2481 3181 11*0 4*884 12*0 4*2001 3003 43*0 d80 d80 4d80 4d80 6482 7*0 7582 19*0 4*2480
  //   12*0 4*24b1 12*0 4*884 12*0 4*2031 44*0 4d80 4d80 d80 d80 28*0 4*2480 12*0 4*24b9 12*0 4*884 12*0
  //   4*2039 92*0 4*24c1 28*0 4*2059 92*0 4*2499 28*0 4*2019 44*0 d80 4d80 d80 4d80 44*0 4*24a1 28*0
  //   4*2021 44*0 4d80 d80 4d80 d80 44*0 4*2491 28*0 4*2011 44*0 f80 4f80 f80 4f80 44*0 4*2489 28*0 4*2009
  //   44*0 4f80 f80 4f80 f80 28*0 4*2480 12*0 4*2481 12*0 4*884 12*0 4*2061 44*0 d80 d80 4d80 4d80 28*0
  //   4*2480 28*0 4*884 60*0 4d80 4d80 d80 d80 28*0 4*2480 12*0 4*24b9 12*0 4*884 108*0 4*24c1 124*0
  //   4*2499 76*0 d80 4d80 d80 4d80 44*0 4*24a9 28*0 4*2029 44*0 4d80 d80 4d80 d80 44*0 4*2491 12*0 4*2489
  //   60*0 f80 4f80 f80 4f80 44*0 4*2489 76*0 4f80 f80 4f80 f80
  //   DON'T CHANGE THE LOCATIONS OF THE INPUTS AND OUTPUTS!
  //   OUTPUT from your circuit
endmodule
