// Logisim project cpu.circ as structural Verilog: 4 circuits, main circuit cpu
module cpu (
  input  clk,
  input  [31:0] INSTRUCTION,
  input  [31:0] READ_DATA,
  output [31:0] WRITE_ADDRESS,
  output [31:0] PROGRAM_COUNTER,
  output [31:0] ra,
  output [31:0] sp,
  output [31:0] t0,
  output [31:0] t1,
  output [31:0] t2,
  output [31:0] s0,
  output [31:0] s1,
  output [31:0] a0,
  output [31:0] tohost,
  output [3:0] WRITE_ENABLE,
  output [31:0] WRITE_DATA
);

  wire ASel, BrEq, BrLt, BrUn, BSel, CSRSel, CSRWen, MemRW, PCSel, RegWEn;
  wire [1:0] WBSel;
  wire [2:0] funct3, ImmSel;
  wire [3:0] ALUSel;
  wire [11:0] csrdecoder_1_csr_addr;
  wire [31:0] csrdecoder_1_csr_data, Imm, inst_reg, MASKED_DATA, multiplexer_1_out, multiplexer_3_out,
       multiplexer_4_out, next_inst, PC_plus4, PC_reg, PC_reg_plus4, Read_Data_1, Write_Data_t;

  Adder #(.width(32)) adder_1 (.a(PROGRAM_COUNTER), .b(32'h4), .out(PC_plus4));  // open: cin, cout
  Multiplexer #(.enable("false"), .width(32)) multiplexer_1 (
    .in0(PC_plus4), .in1(WRITE_ADDRESS), .out(multiplexer_1_out), .sel(PCSel));
  Register #(.width(32)) PC (.D(multiplexer_1_out), .clk(clk), .Q(PROGRAM_COUNTER));  // open: en, clr
  Multiplexer #(.enable("false"), .width(32)) multiplexer_2 (
    .in0(INSTRUCTION), .in1(32'h13), .out(next_inst), .sel(PCSel));
  Register #(.width(32)) register_1 (
    .D(next_inst), .clk(clk), .Q({inst_reg[31:15], funct3, inst_reg[11:0]}));  // open: en, clr
  Register #(.width(32)) register_2 (.D(PROGRAM_COUNTER), .clk(clk), .Q(PC_reg));  // open: en, clr
  imm_gen imm_gen_1 (.inst({inst_reg[31:15], funct3, inst_reg[11:0]}), .ImmSel(ImmSel), .imm(Imm));
  control_logic control_logic_1 (
    .CSRWen(CSRWen), .PCSel(PCSel), .RegWEn(RegWEn), .ImmSel(ImmSel), .BrUn(BrUn), .ASel(ASel), .BSel(BSel),
    .ALUSel(ALUSel), .MemRW(MemRW), .WBSel(WBSel), .CSRSel(CSRSel),
    .inst({inst_reg[31:15], funct3, inst_reg[11:0]}), .BrEq(BrEq), .BrLt(BrLt));
  branch_comp branch_comp_1 (.rs1(Read_Data_1), .rs2(WRITE_DATA), .BrUn(BrUn), .BrEq(BrEq), .BrLt(BrLt));
  regfile regfile_1 (
    .rs1(inst_reg[19:15]), .rs2(inst_reg[24:20]), .rd(inst_reg[11:7]), .Write_Data(Write_Data_t),
    .RegWEn(RegWEn), .clk(clk), .ra(ra), .sp(sp), .t0(t0), .t1(t1), .t2(t2), .s0(s0), .s1(s1), .a0(a0),
    .Read_Data_1(Read_Data_1), .Read_Data_2(WRITE_DATA));
  csrDecoder csrdecoder_1 (
    .inst({inst_reg[31:15], funct3, inst_reg[11:0]}), .rs1(Read_Data_1), .CSRSel(CSRSel),
    .csr_addr(csrdecoder_1_csr_addr), .csr_data(csrdecoder_1_csr_data));
  Multiplexer #(.enable("false"), .width(32)) multiplexer_3 (
    .in0(Read_Data_1), .in1(PC_reg), .out(multiplexer_3_out), .sel(ASel));
  Multiplexer #(.enable("false"), .width(32)) multiplexer_4 (
    .in0(WRITE_DATA), .in1(Imm), .out(multiplexer_4_out), .sel(BSel));
  csr csr_1 (
    .CSR_address(csrdecoder_1_csr_addr), .CSR_din(csrdecoder_1_csr_data), .CSR_WE(CSRWen), .clk(clk),
    .tohost(tohost));
  alu alu_1 (.Result(WRITE_ADDRESS), .A(multiplexer_3_out), .B(multiplexer_4_out), .ALUSel(ALUSel));
  Adder #(.width(32)) adder_2 (.a(PC_reg), .b(32'h4), .out(PC_reg_plus4));  // open: cin, cout
  maskGenerator maskgenerator_1 (.funct3(funct3), .writeEn(MemRW), .write_enable(WRITE_ENABLE));
  maskRead maskread_1 (.funct3(funct3), .readData(READ_DATA), .outData(MASKED_DATA));
  Multiplexer #(.enable("false"), .select(2), .width(32)) multiplexer_5 (
    .in0(MASKED_DATA), .in1(WRITE_ADDRESS), .in2(PC_reg_plus4), .in3(Imm), .out(Write_Data_t), .sel(WBSel));

  // Other names for the same wires on the sheet: ALU_res[31:0] = WRITE_ADDRESS; inst_reg[14:12] = funct3;
  //   Read_Data_2[31:0] = WRITE_DATA

  // Notes on the sheet:
  //   The instruction at PC + 4
  //   nop instruction
  //   Output to IMEM
  //   Additional registers are requested in double cycle CPU
  //   IMEM (do **NOT** move this)
  //   Inputs from IMEM
  //   PC_reg is used for calculating the address where to jump, if the branch or jump is taken.
  //   Note: PCSel is TRUE, only when the brach is taken or the instruction being execued is J-type.
  //   It is OK to move the PC, RegFile, ALU, MEM, Branch Comp, Imm Gen, and Control Logic to wherever is most convenient for you when constructing your CPU, and to delete this text
  //   Inputs/Outputs for testing. Do **NOT** move these.
  //   Outputs To DMEM
  //   DMEM (do **NOT** move this)
  //   Inputs From DMEM
  //   The data to be written to memory
endmodule

module csrDecoder (
  input  [31:0] inst,
  input  [31:0] rs1,
  input  CSRSel,
  output [11:0] csr_addr,
  output [31:0] csr_data
);

  wire [31:0] csr_imm;

  assign csr_imm = {{27{1'b0}}, inst[19:15]};  // Bit_Extender bit_extender_1
  Multiplexer #(.enable("false"), .width(32)) multiplexer_1 (.in0(rs1), .in1(csr_imm), .out(csr_data), .sel(CSRSel));

  assign csr_addr = inst[31:20];

  // Other names for the same wires on the sheet: INSTRUCTION[31:0] = inst

  // Notes on the sheet:
  //   Input
  //   Output
endmodule

module maskGenerator (
  input  [2:0] funct3,
  input  writeEn,
  output [3:0] write_enable
);

  wire [3:0] multiplexer_1_out;

  Multiplexer #(.enable("false"), .select(2), .width(4)) multiplexer_1 (
    .in0(4'b0001), .in1(4'b0011), .in2(4'b1111), .out(multiplexer_1_out), .sel(funct3[1:0]));  // open: in3
  Multiplexer #(.enable("false"), .width(4)) multiplexer_2 (
    .in0(4'b0000), .in1(multiplexer_1_out), .out(write_enable), .sel(writeEn));

  // Other names for the same wires on the sheet: mask[3:0] = write_enable

  // Notes on the sheet:
  //   Input
  //   Output
endmodule

module maskRead (
  input  [2:0] funct3,
  input  [31:0] readData,
  output [31:0] outData
);

  wire [31:0] lb, lh;

  assign lb = {{24{readData[7]}}, readData[7:0]};  // Bit_Extender bit_extender_1
  assign lh = {{16{readData[15]}}, readData[15:0]};  // Bit_Extender bit_extender_2
  Multiplexer #(.enable("false"), .select(3), .width(32)) multiplexer_1 (
    .in0(lb), .in1(lh), .in2(readData), .out(outData), .sel(funct3));  // open: in3, in4, in5, in6, in7

  // Notes on the sheet:
  //   Input
  //   Output
endmodule
