// Logisim project imm_gen.circ as structural Verilog: 2 circuits, main circuit imm_gen
module imm_gen (
  input  [31:0] inst,
  input  [2:0] ImmSel,
  output [31:0] imm
);

  immediate_generator immediate_generator_1 (.inst(inst), .ImmSel(ImmSel), .imm(imm));

  // Notes on the sheet:
  //   INPUTS to your circuit
  //   DON'T CHANGE THE LOCATIONS OF THE INPUTS AND OUTPUTS!
  //   OUTPUT from your circuit
endmodule

module immediate_generator (
  input  [31:0] inst,
  input  [2:0] ImmSel,
  output [31:0] imm
);

  wire [31:0] I, S, SB, UJ;

  Multiplexer #(.enable("false"), .select(3), .width(32)) multiplexer_1 (
    .in1(I), .in2(S), .in3(SB), .in4({inst[31:12], {12{1'b0}}}), .in5(UJ), .out(imm), .sel(ImmSel));  // open: in0, in6, in7
  assign I = {{20{inst[31]}}, inst[31:20]};  // Bit_Extender bit_extender_1
  assign S = {{20{inst[31]}}, {inst[31:25], inst[11:7]}};  // Bit_Extender bit_extender_2
  assign SB = {{19{inst[31]}}, {inst[31], inst[7], inst[30:25], inst[11:8], 1'b0}};  // Bit_Extender bit_extender_3
  assign UJ = {{11{inst[31]}}, {inst[31], inst[19:12], inst[20], inst[30:21], 1'b0}};  // Bit_Extender bit_extender_4

  // Other names for the same wires on the sheet: bit8_11[3:0] = inst[11:8]; s_type[11:0] = {inst[31:25], inst[11:7]};
  //   sb_type[12:1] = {inst[31], inst[7], inst[30:25], inst[11:8]}; bit7 = inst[7]; bit21_24[3:0] = inst[24:21];
  //   i_type[11:0] = inst[31:20]; U[31:12] = inst[31:12];
  //   uj_type[20:1] = {inst[31], inst[19:12], inst[20], inst[30:21]}; bit25_30[5:0] = inst[30:25]; bit20 = inst[20];
  //   bit12_19[7:0] = inst[19:12]; bit31 = inst[31]

  // Notes on the sheet:
  //   Step 1: Bit Extraction
  //   Step 3: Bit Selection
  //   Output
  //   Step 2: Bit Extention
endmodule
